# Fritzing sketch BT_HC-05 (saved by Fritzing 0.9.3b)
breadboards: 1

parts:
  Composant1 = Arduino Uno (Rev3)
  Composant2 = Bluetooth HC-05 Macho  # not connected
  LED1 = LED - 5mm [color="Blue (505nm)" package="5 mm [THT]"]

nets:
  N1: Composant1.GND, LED1.cathode

notes:
  HC-08
  STATE : LED
  RXD : D10
  TXD : D11
  GND : GND
  VCC : 5V
  EN(KEY) : D9

// code stored in the sketch: BT_HC-05.ino
#include <SoftwareSerial.h>
int vitesse =38400;
SoftwareSerial BTSerial(10, 11);// RX TX
void setup()
{  
  pinMode(9,OUTPUT);
  pinMode(10,INPUT);
  pinMode(11,OUTPUT);
 
  digitalWrite(9,HIGH);
 // digitalWrite(10,LOW);

  Serial.begin(vitesse);
  
  BTSerial.begin(vitesse);
  BTSerial.write("AT\n\r");
}
void loop()
{
  
  Serial.begin(vitesse);  
  BTSerial.begin(vitesse);
  BTSerial.write("AT \n \r");
   delay(1000);
  BTSerial.write("AT \r \n");
  delay(1000);
 Serial.println(vitesse);
  
  if(BTSerial.available())
  {
     Serial.println(vitesse);
    Serial.println(BTSerial.read());
  }
//  else
//  vitesse =vitesse*2;

  if(Serial.available())
    BTSerial.write(Serial.read());
}
