# Fritzing sketch BT_HC-08 (saved by Fritzing 0.9.3b)
breadboards: 1

parts:
  Composant1 = Arduino Uno (Rev3)
  Composant2 = Bluetooth HC-05 Macho  # not connected
  LED1 = LED - 5mm [color="Blue (430nm)" package="5 mm [THT]"]
  LED2 = LED - 5mm [color="Red (633nm)" package="5 mm [THT]"]

nets:
  N1: Composant1.D9_PWM, Composant1.GND, LED1.cathode, LED2.anode

notes:
  HC-08
  STATE : LED bleue
  RXD : D11 (Tx Arduino)
  TXD : D10 (RX Arduino)
  GND : GND
  VCC : D12 (Gestion mode AT)
  EN(KEY) : D9 (Gestion mode AT)
  LED rouge (mode AT)

// code stored in the sketch: BT_HC-08_TMP.ino
#include <SoftwareSerial.h>
int vitesse = 9600;//vitesse terminal
int vitesseBT = 9600;//vitesse BT
int boucle = 0; // pour compter le nombre de commandes renvoyées par BT
char ATplus[] = "pat";  //mot clé pour mise en mode AT
char ATmoins[] = "mat";//mot clé pour sortir du mode  en AT
char ATvit[] = "vit";//mot clé pour forcer la vitesse BT

SoftwareSerial BTSerial(10, 11);
void setup() {
  // put your setup code here, to run once:
  Serial.begin(vitesse);
  BTSerial.begin(vitesseBT);
  
  pinMode(9, OUTPUT);//EN
  pinMode(10, INPUT );//RX
  pinMode(11, OUTPUT);//TX
  pinMode(12, OUTPUT);//VCC

  mise_en_AT();
  BTSerial.write("AT");
  sortie_AT();
  Serial.println("c'est parti!");
  Serial.flush();
}

void loop() {
  // put your main code here, to run repeatedly:

  int combienBT = BTSerial.available();  // on scrute les message de BT
  if (combienBT > 0)
  {
    Serial.print("boucle : ");
    Serial.print(boucle);
    Serial.print(" taille :  ");
    Serial.println(combienBT);
    Serial.print(" vitesse : ");
    Serial.println(vitesse);
    for (int i = 0; i < combienBT; i++)
      Serial.print(BTSerial.read(),DEC);
    boucle = boucle + 1;
    Serial.println();
  }

  int combienS = 0;   // on parle à BT
  combienS = Serial.available();

  if (combienS != 0)    //quelque chose d'envoyé
  {
    Serial.print(" combien Serie : ");
    Serial.println(combienS);
    if (combienS == 5) //surement un mot clé
    {
      char entree[3];
      for (int i = 0; i < 3; i++) {
        entree[i] = Serial.read(); delay(5);
      }

      Serial.print(" entree : ");
      Serial.println(entree);
      
      if   (*ATplus == *entree )
      {        
        mise_en_AT();
      }
      else if (*ATmoins == *entree)
      {        
        sortie_AT();
      }
      else if (*ATvit == *entree) //pour changer la vitesse
      {
        Serial.println("Vitesse : ");
        char VITESSE_BUFFER[8];
        for (int i = 0; i < 8; i++)
          VITESSE_BUFFER[i] = Serial.read();
        vitesse = atoi(VITESSE_BUFFER);
        Serial.println(vitesse);
      }
      else // c'était pas un mot clé
      {
        BTSerial.print(entree);
        //Serial.print(entree);
        char c;
        while (Serial.available())
        {
          c = Serial.read();
          BTSerial.print(c);          
        }       
      }
    }
    else // un truc à faire envoyer par BT  
    {
      char c;
      while (Serial.available())
      {
        c = Serial.read();
        BTSerial.write(c);       
      }
    }
    Serial.println();
  } 
  delay(500);
  
}

void mise_en_AT()
{
  Serial.println("mise_en_AT");
  digitalWrite(10, LOW);
  digitalWrite(11, LOW);
  digitalWrite(12, LOW);
  digitalWrite(9, HIGH);
  delay(3000);
  digitalWrite(12, HIGH);
  delay(200);
}

void sortie_AT()
{
  Serial.println("sortie_AT");
  digitalWrite(10, LOW);
  digitalWrite(11, LOW);
  digitalWrite(12, LOW);
  digitalWrite(9, LOW);
  delay(3000);
  digitalWrite(12, HIGH);
  delay(200);
}
